# Fritzing sketch Arduino-Temp-Logger (saved by Fritzing 0.9.1b)
breadboards: 1

parts:
  U1 = Mystery Part - 3 pins [chip_label=DS18B20 package=THT]
  Part1 = Real Time Clock Module - DS1307 RTC Breakout Board
  U2 = RF-LINK_TX [package=rf-link_tx]
  ANT1 = Antenna
  R1 = Resistor [tolerance=±5% resistance=4.7k package=THT]
  Part2 = Arduino Uno (Rev3)

nets:
  GND: U1.pin1, U1.pin3, Part1.GND, U2.GND, Part2.GND
  N1: U1.pin2, R1.Pin_0, Part2.D2
  5V: Part1.5V, U2.+5V, R1.Pin_1, Part2.5V
  N2: Part1.SCL, Part2.A5/SCL
  N3: Part1.SDA, Part2.A4/SDA
  N4: U2.ANT, ANT1.antenna_lead
  N5: U2.DATA, Part2.D12/MISO

custom parts:
  Mystery Part - 3 pins: A dummy, proxy, ersatz, stand-in part for whatever you want. With 3 pins on a 100 mil inline pin header footprint.
